# Fritzing sketch circuit (saved by Fritzing 0.9.2b)
breadboards: 1

parts:
  Eleman1 = Arduino Mega 2560 (Rev3)
  R1 = Rotary Potentiometer (Small) [maximum_resistance=100kΩ package=THT]
  Eleman2 = blueIOT RevB
  Eleman3 = blueIOT RevB
  U2 = 74HC4052 [package=dil16]
  LCD1 = LCD screen

nets:
  N1: Eleman1.D21/SCL, U2.Y
  N2: Eleman1.D20/SDA, U2.X
  3V3: Eleman1.3V3, Eleman2.3V3, Eleman3.3V3
  5V: Eleman1.5V, R1.leg2, U2.VCC, LCD1.VDD, LCD1.LED+
  GND: Eleman1.GND, R1.leg1, Eleman2.GND, Eleman3.GND, U2.INH, U2.VEE, U2.GND, U2.B, LCD1.VSS, LCD1.R/W, LCD1.LED-
  N3: Eleman1.D30, U2.A
  N4: Eleman1.D35, LCD1.DB7
  N5: Eleman1.D37, LCD1.DB6
  N6: Eleman1.D39, LCD1.DB5
  N7: Eleman1.D41, LCD1.DB4
  N8: Eleman1.D43, LCD1.E
  N9: Eleman1.D45, LCD1.RS
  N10: R1.wiper, LCD1.V0
  N11: Eleman2.SCA/A4, U2.X1
  N12: Eleman2.SCL/A5, U2.Y1
  N13: Eleman3.SCA/A4, U2.X0
  N14: Eleman3.SCL/A5, U2.Y0

notes:
  SDA-1
  SCL-1
  SDA-2
  SCL-2
  DATA BITS 7-4
  Enable
  RS
  E
  M
  R
  A
  Y
